# Fritzing sketch Main_Flight_Computer (saved by Fritzing 0.9.4)

parts:
  Parça1 = Arduino Mega ADK (Rev3)
  LED1 = smd LED [color="Red (633nm)" package="0805 [SMD]"]
  J1 = Piezo Speaker
  microSD1 = MicroSD Card Module
  M1 = gy9250
  GY-NEO6MV2 = SUP500F [package=sup500f]
  BAT1 = 18650 battery holder [package=battery-18650-kit]
  BAT2 = 18650 battery holder [package=battery-18650-kit]
  Reg1 = DC-DC CONVERTER [part_number=80633 package=dc-dc_converter]
  S1 = Pushbutton [package="[THT]"]
  Parça4 = NRF24L01+ Breakout Board
  BMP280_Breakout1 = BMP280 Breakout Board [part_number=BMP280]
  2_Channel_Relay1 = 2 Channel Power Relay
  R1 = Resistor [tolerance=±5% resistance=220 package="0603 [SMD]"]
  R2 = Resistor [tolerance=±5% resistance=0 package=THT]

nets:
  N1: Parça1.D21/SCL, BMP280_Breakout1.SCL
  N2: Parça1.D20/SDA, BMP280_Breakout1.SDA
  N3: Parça1.D17/RX2, GY-NEO6MV2.GND
  N4: Parça1.D16/TX2, GY-NEO6MV2.VCC
  GND: Parça1.GND, LED1.cathode, J1.pin1, microSD1.GND, M1.pin2, GY-NEO6MV2.RX-I, Reg1.OUT-, Parça4.GND, BMP280_Breakout1.GND, 2_Channel_Relay1.GND
  N5: Parça1.D8_PWM, Parça4.CS
  VCC: Parça1.3V3, Parça4.VCC, BMP280_Breakout1.VCC
  VCC_2: Parça1.5V, microSD1.VCC, M1.pin1, GY-NEO6MV2.TX-O, 2_Channel_Relay1.VCC
  N6: Parça1.VIN, Reg1.OUT+
  N7: Parça1.D7_PWM, Parça4.CE
  N8: Parça1.D23, 2_Channel_Relay1.IN2
  N9: Parça1.D25, 2_Channel_Relay1.IN1
  N10: Parça1.D47, R1.Pin_1
  N11: Parça1.D49, J1.pin2
  N12: Parça1.D50/MISO, Parça4.MISO
  N13: Parça1.D51/MOSI, Parça4.MOSI
  N14: Parça1.D52/SCK, Parça4.SCK
  N15: Parça1.D53/SS, microSD1.CS
  N16: LED1.anode, R1.Pin_0
  N17: BAT1.+, BAT2.+, Reg1.IN+, S1.Pin_3, S1.Pin_4
  N18: BAT1.-, BAT2.-, Reg1.IN-, S1.Pin_1, S1.Pin_2
  N19: 2_Channel_Relay1.K2-COM, R2.Pin_0

notes:
  GND:Black
  VCC: Red
  RX: Yellow
  TX: Green

custom parts:
  gy9250: MPU-9250 module (three-axis gyroscope + three-axis acceleration + three-axis magnetic field). The generic model from ebay et. al. rather than the Sparkfun version.
  18650 battery holder: 18650 Battery Holder
  DC-DC CONVERTER: WYHP 5A constant current/voltage manufactured by Shenzhen Weiyapuhua Technology Co., Ltd
  BMP280 Breakout Board: This is a breakout board for the Bosch Sensortec BMP280, "an absolute barometric pressure sensor especially designed for mobile applications." The operation range is 300 to 1100 hPa. Supply voltage is 1.2 to 3.6V. Operating temperature range is -40 to +85 °C.
  2 Channel Power Relay: A 2 channel power relay. The module operates at 5V.
